# Fritzing sketch Model (saved by Fritzing 0.9.3b)
breadboards: 1

parts:
  Part1 = Arduino Uno (Rev3)
  LED1 = smd LED [color="Blue (430nm)" package="1206 [SMD]"]
  LED2 = smd LED [color="Red (633nm)" package="1206 [SMD]"]
  R1 = Resistor [tolerance=±5% resistance=220 package="2010 [SMD]"]
  R2 = Resistor [tolerance=±5% resistance=220 package="2010 [SMD]"]
  R3 = Photocell (LDR) [package=THT]
  R4 = Resistor [tolerance=±5% resistance=1k package="2010 [SMD]"]
  J1 = Piezo Speaker
  U1 = LCD-16X2 [package=lcd-16x2_noholes]
  R5 = Resistor [tolerance=±5% resistance=1k package="2010 [SMD]"]
  R6 = Trimmer Potentiometer [maximum_resistance=10kΩ package=THT]
  Part3 = Bluetooth HC-05 Macho  # not connected
  Part4 = Bluetooth HC-05 Macho  # not connected
  Part5 = KY-013 Analog Temperature Sensor Module [package="Breakout board"]

nets:
  N1: Part1.A1, R3.pin_1, R4.Pin_0
  N2: Part1.A2, Part5.S
  N3: Part1.D10_PWM/SS, J1.pin2
  N4: Part1.D12/MISO, R2.Pin_1
  N5: Part1.D13/SCK, R1.Pin_0
  GND: Part1.GND, LED1.cathode, LED2.cathode, R4.Pin_1, J1.pin1, U1.VSS, U1.R_W, U1.K, Part5.Vin
  N6: Part1.D2, U1.DB7
  N7: Part1.D3_PWM, U1.DB6
  N8: Part1.D4, U1.DB5
  N9: Part1.D5_PWM, U1.DB4
  N10: Part1.D6_PWM, U1.E
  N11: Part1.D7, U1.RS
  5V: Part1.5V, R3.pin_0, U1.VDD, R5.Pin_1, R6.leg1, Part5.-
  N12: LED1.anode, R1.Pin_1
  N13: LED2.anode, R2.Pin_0
  N14: U1.VO, R6.wiper
  N15: U1.A, R5.Pin_0

custom parts:
  KY-013 Analog Temperature Sensor Module: KY-013 Analog Temperature Sensor module, measures ambient temperature based on resistance of the thermistor.
